# Fritzing sketch counter_with_button (saved by Fritzing 0.9.4)
breadboards: 1

parts:
  R1 = Resistor [tolerance=±5% resistance=220 package=THT]
  S1 = Pushbutton [package="[THT]"]
  LED1 = LED - 5mm [color="Red (633nm)" package="5 mm [THT]"]
  Parça1 = Arduino Uno (Rev3)
  S2 = Pushbutton [package="[THT]"]
  S3 = Pushbutton [package="[THT]"]
  R2 = Resistor [tolerance=±5% resistance=10k package=THT]
  R4 = Resistor [tolerance=±5% resistance=10k package=THT]

nets:
  N1: R1.Pin_0, Parça1.D8
  N2: R1.Pin_1, LED1.anode
  N3: S1.Pin_1, S1.Pin_2, Parça1.D6_PWM, R2.Pin_1
  N4: S1.Pin_3, S1.Pin_4, Parça1.5V, S2.Pin_3, S2.Pin_4
  N5: LED1.cathode, Parça1.GND, S3.Pin_3, S3.Pin_4, R2.Pin_0, R4.Pin_0
  N6: Parça1.D7, S2.Pin_1, S2.Pin_2, R4.Pin_1
  N7: Parça1.RESET, S3.Pin_1, S3.Pin_2
