# Fritzing sketch led_level_with_pwm_pins (saved by Fritzing 0.9.4)
breadboards: 1

parts:
  Parça1 = Arduino Uno (Rev3)
  LED2 = LED - 5mm [color="Red (633nm)" package="5 mm [THT]"]
  R1 = Resistor [tolerance=±5% resistance=220 package=THT]

nets:
  N1: Parça1.D3_PWM, R1.Pin_0
  N2: LED2.anode, R1.Pin_1
