# Fritzing sketch sliding_leds_with_button (saved by Fritzing 0.9.4)
breadboards: 1

parts:
  Parça1 = Arduino Uno (Rev3)
  R1 = Resistor [tolerance=±5% resistance=220 package="0603 [SMD]"]
  R2 = Resistor [tolerance=±5% resistance=220 package="0603 [SMD]"]
  R3 = Resistor [tolerance=±5% resistance=220 package="0603 [SMD]"]
  R4 = Resistor [tolerance=±5% resistance=220 package="0603 [SMD]"]
  S2 = Pushbutton [package="[SMD]"]
  S3 = Pushbutton [package="[SMD]"]
  LED1 = smd LED [color="Red (633nm)" package="1206 [SMD]"]
  LED2 = smd LED [color="Red (633nm)" package="1206 [SMD]"]
  LED3 = smd LED [color="Red (633nm)" package="1206 [SMD]"]
  LED4 = smd LED [color="Red (633nm)" package="1206 [SMD]"]
  LED5 = smd LED [color="Red (633nm)" package="1206 [SMD]"]
  LED6 = smd LED [color="Red (633nm)" package="1206 [SMD]"]
  LED7 = smd LED [color="Red (633nm)" package="1206 [SMD]"]
  LED8 = smd LED [color="Red (633nm)" package="1206 [SMD]"]
  LED9 = smd LED [color="Red (633nm)" package="1206 [SMD]"]
  LED10 = smd LED [color="Red (633nm)" package="1206 [SMD]"]
  R5 = Resistor [tolerance=±5% resistance=220 package="0603 [SMD]"]
  R6 = Resistor [tolerance=±5% resistance=220 package="0603 [SMD]"]
  R7 = Resistor [tolerance=±5% resistance=220 package="0603 [SMD]"]
  R8 = Resistor [tolerance=±5% resistance=220 package="0603 [SMD]"]
  R9 = Resistor [tolerance=±5% resistance=220 package="0603 [SMD]"]
  R10 = Resistor [tolerance=±5% resistance=220 package="0603 [SMD]"]
  R11 = Resistor [tolerance=±5% resistance=10k package="0603 [SMD]"]
  R12 = Resistor [tolerance=±5% resistance=10k package="0603 [SMD]"]

nets:
  N1: Parça1.D8, R7.Pin_0
  N2: Parça1.D9_PWM, R8.Pin_0
  N3: Parça1.D10_PWM/SS, R9.Pin_0
  N4: Parça1.D11_PWM/MOSI, R10.Pin_0
  N5: Parça1.D12/MISO, S3.Pin_1, S3.Pin_2, R12.Pin_0
  N6: Parça1.D13/SCK, S2.Pin_1, S2.Pin_2, R11.Pin_0
  N7: Parça1.D2, R1.Pin_0
  N8: Parça1.D3_PWM, R4.Pin_0
  N9: Parça1.D4, R2.Pin_0
  N10: Parça1.D5_PWM, R3.Pin_0
  N11: Parça1.D6_PWM, R6.Pin_0
  N12: Parça1.D7, R5.Pin_0
  N13: Parça1.GND, LED1.cathode, LED2.cathode, LED3.cathode, LED4.cathode, LED5.cathode, LED6.cathode, LED7.cathode, LED8.cathode, LED10.cathode, R11.Pin_1, R12.Pin_1
  N14: R1.Pin_1, LED1.anode
  N15: R2.Pin_1, LED3.anode
  N16: R3.Pin_1, LED4.anode
  N17: R4.Pin_1, LED2.anode
  N18: S2.Pin_3, S2.Pin_4
  N19: S3.Pin_3, S3.Pin_4
  N20: LED5.anode, R6.Pin_1
  N21: LED6.anode, R5.Pin_1
  N22: LED7.anode, R7.Pin_1
  N23: LED8.anode, R8.Pin_1
  N24: LED9.anode, R9.Pin_1
  N25: LED10.anode, R10.Pin_1
